# Fritzing sketch pragoPi (saved by Fritzing 0.9.3b)

parts:
  MCU1 = Raspberry Pi Zero
  DC-DC_Upscaler = RioRand LM2596
  Watch_movement = DC Motor
  L298_Module = H-Bridge with L298N
  2N2222 = TRANSISTOR_NPN [package=to-92-ammo]
  R1 = Resistor [tolerance=±5% resistance=1k package=THT]

nets:
  N1: MCU1.pin_2, MCU1.pin_4, DC-DC_Upscaler.Pin_1, 2N2222.E
  N2: MCU1.pin_6, DC-DC_Upscaler.Pin_2
  N3: MCU1.pin_16, L298_Module.IN1
  N4: MCU1.pin_18, L298_Module.IN2
  N5: MCU1.pin_22, R1.Pin_0
  N6: DC-DC_Upscaler.Pin_3, L298_Module.12V
  N7: DC-DC_Upscaler.Pin_4, L298_Module.GND
  N8: Watch_movement.pin_1, L298_Module.OUT1-Motor1
  N9: Watch_movement.pin_2, L298_Module.OUT2-Motor1
  N10: L298_Module.5V, 2N2222.C
  N11: 2N2222.B, R1.Pin_1

custom parts:
  H-Bridge with L298N: h-bridge
